# Fritzing sketch sismo_alerta (saved by Fritzing 0.8.7b)
breadboards: 1

parts:
  PART1 = Polymer Lithium Ion Battery - Generic
  Part1 = Arduino Pro Mini v13
  R1 = Resistor [tolerance=±5% resistance=10M package=THT]
  LED1 = LED - 5mm [color="Red (633nm)" package="5 mm [THT]"]
  LED2 = LED - 5mm [color="Green (555nm)" package="5 mm [THT]"]
  J1 = Piezo Speaker
  S2 = Pushbutton [package="[THT]"]
  S3 = Pushbutton [package="[THT]"]
  R2 = Resistor [tolerance=±5% resistance=10M package=THT]
  LED3 = LED - 5mm [color="Red (633nm)" package="5 mm [THT]"]
  LED4 = LED - 5mm [color="Green (555nm)" package="5 mm [THT]"]
  R3 = Resistor [tolerance=±5% resistance=33 package=THT]
  R4 = Resistor [tolerance=±5% resistance=330 package=THT]
  R5 = Resistor [tolerance=±5% resistance=33 package=THT]
  R6 = Resistor [tolerance=±5% resistance=330 package=THT]
  PART4 = Power Cell - LiPo Charger/Booster [part_number=PRT-11231]
  Part2 = Digital FM Radio Receiver

nets:
  N1: PART1.VCC, PART4.JST_+
  N2: PART1.GND, PART4.JST_-
  N3: Part1.A4, Part2.SDIO
  N4: Part1.A5, Part2.!SEN, Part2.SCLK
  GND: Part1.GND, R1.Pin_1, LED1.cathode, LED2.cathode, J1.pin1, S2.Pin_3, S2.Pin_4, S3.Pin_3, S3.Pin_4, LED3.cathode, LED4.cathode, PART4.GND, Part2.GND
  VCC: Part1.VCC, PART4.VCC, Part2.3.3V
  N5: Part1.A0, R1.Pin_0, R2.Pin_0
  N6: Part1.D12/MISO, J1.pin2
  N7: Part1.D10_PWM/SS, Part2.GPIO1, Part2.!RST
  N8: Part1.D9_PWM, R3.Pin_0
  N9: Part1.D8, R4.Pin_0
  N10: Part1.D7, R5.Pin_0
  N11: Part1.D6_PWM, R6.Pin_0
  N12: Part1.D5_PWM, S2.Pin_1, S2.Pin_2
  N13: Part1.RESET, S3.Pin_1, S3.Pin_2
  N14: LED1.anode, R4.Pin_1
  N15: LED2.anode, R3.Pin_1
  N16: R2.Pin_1, PART4.5V
  N17: LED3.anode, R6.Pin_1
  N18: LED4.anode, R5.Pin_1

custom parts:
  Polymer Lithium Ion Battery - Generic: Description: These are batteries based on the new Polymer Lithium Ion chemistry. This is the highest energy density currently in production. Comes terminated with a standard 2-pin JST-PH connector - 2mm spacing between pins. These batteries require special charging. Do not attempt to charge these with anything but a specialized LiPo charger. Battery includes built-in protection against over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
  Power Cell - LiPo Charger/Booster: The PowerCell board is a single cell LiPo boost converter (to 3.3V and 5V) and micro-USB charger in one. The board comes with a JST connector for a single cell LiPo battery, a micro-USB connector for the 5V charge input, and selectable 3.3V and 5V output pins (labeled 'out'). There are also two charge pins broken out (labeled 'charge'), so you can use another 5V power source to charge the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
